# Fritzing sketch DiscoHat (saved by Fritzing 0.9.2b)
circuit board: 8.46667cm x 5.64444cm

parts:
  Part1 = Arduino Due (Rev2b)
  R1 = Resistor [tolerance=±5% resistance=220 package=THT]
  R2 = Resistor [tolerance=±5% resistance=220 package=THT]
  R3 = Resistor [tolerance=±5% resistance=220 package=THT]
  R4 = Resistor [tolerance=±5% resistance=220 package=THT]
  R5 = Resistor [tolerance=±5% resistance=220 package=THT]
  R6 = Resistor [tolerance=±5% resistance=220 package=THT]
  R7 = Resistor [tolerance=±5% resistance=220 package=THT]
  R8 = Resistor [tolerance=±5% resistance=220 package=THT]
  R9 = Resistor [tolerance=±5% resistance=220 package=THT]
  R10 = Resistor [tolerance=±5% resistance=220 package=THT]
  LED2 = LEDs [package=led10mm]
  LED1 = LEDs [package=led10mm]
  LED3 = LEDs [package=led10mm]
  LED5 = LEDs [package=led10mm]
  LED6 = LEDs [package=led10mm]
  LED7 = LEDs [package=led10mm]
  LED8 = LEDs [package=led10mm]
  LED9 = LEDs [package=led10mm]
  LED10 = LEDs [package=led10mm]
  LED11 = LEDs [package=led10mm]

nets:
  N1: Part1.D8_PWM, LED5.C
  N2: Part1.D9_PWM, LED6.C
  N3: Part1.D10_PWM/SS0, LED3.C
  N4: Part1.D11_PWM, LED2.C
  N5: Part1.D12_PWM, LED1.C
  N6: Part1.GND, R1.Pin_0, R2.Pin_0, R3.Pin_0, R4.Pin_0, R5.Pin_0, R6.Pin_0, R7.Pin_0, R8.Pin_0, R9.Pin_0, R10.Pin_0
  N7: Part1.D3_PWM, LED11.C
  N8: Part1.D4_PWM/SS1, LED10.C
  N9: Part1.D5_PWM, LED9.C
  N10: Part1.D6_PWM, LED8.C
  N11: Part1.D7_PWM, LED7.C
  N12: R1.Pin_1, LED10.A
  N13: R2.Pin_1, LED9.A
  N14: R3.Pin_1, LED8.A
  N15: R4.Pin_1, LED11.A
  N16: R5.Pin_1, LED7.A
  N17: R6.Pin_1, LED5.A
  N18: R7.Pin_1, LED6.A
  N19: R8.Pin_1, LED3.A
  N20: R9.Pin_1, LED2.A
  N21: R10.Pin_1, LED1.A

// code stored in the sketch: DiscoHat.ino
void setup() {
  //BLUE
  pinMode(3, OUTPUT);
  pinMode(4, OUTPUT);
  pinMode(5, OUTPUT);
  pinMode(6, OUTPUT);
  pinMode(7, OUTPUT);
  //RED
  pinMode(8, OUTPUT);
  pinMode(9, OUTPUT);
  pinMode(10, OUTPUT); 
  pinMode(11, OUTPUT);
  pinMode(12, OUTPUT);
}
// the loop function runs over and over again forever
void loop() {
  //fade(5);
  colorsInParallel();
  colorsInParallel();
  colorsInParallel();
  colorsInParallel();
  
  colorsInSequence();
  colorsInSequence();
  colorsInSequence();
  colorsInSequence();
  
  allInSequence();
  allInSequence();
  allInSequence();
  allInSequence();
  allInSequence();
}
// DIFFERENT PROGRAMS
// all blue are on, then all red and so on
void colorsInParallel(){
  blueon();
  redon();
  delay(1000);              // wait for a second
  blueoff();
  redoff();
  delay(750);              // wait for a second
}
// all blue are on, then all red and so on
void colorsInSequence(){
  blueon();
  delay(750);              // wait for a second
  blueoff();
  redon();
  delay(750);              // wait for a second
  redoff();
}
// LEDs are turnd of in sequence
void allInSequence() {
  digitalWrite(3, HIGH);
  delay(100);
  digitalWrite(3, LOW);  
  digitalWrite(8, HIGH);
  delay(100);
  digitalWrite(8, LOW);  
  digitalWrite(4, HIGH);
  delay(100);
  digitalWrite(4, LOW);  
  digitalWrite(9, HIGH);
  delay(100);
  digitalWrite(9, LOW);  
  digitalWrite(5, HIGH);
  delay(100);
  digitalWrite(5, LOW);  
  digitalWrite(10, HIGH);
  delay(100);
  digitalWrite(10, LOW);  
  digitalWrite(6, HIGH);
  delay(100);
  digitalWrite(6, LOW);  
  digitalWrite(11, HIGH);
  delay(100);
  digitalWrite(11, LOW);  
  digitalWrite(7, HIGH);
  delay(100);
  digitalWrite(7, LOW);  
  digitalWrite(12, HIGH);
  delay(100);
  digitalWrite(12, LOW);  
}

void fade(int completeFades) {  
  int brightness = 0;
  int fadeAmount = 5;

  while (completeFades > 0) {
    // Set the led brightness
    blueSet(brightness);
    redSet(brightness);
    
    // change the brightness for next time through the loop:
    brightness = brightness + fadeAmount;
  
    // reverse the direction of the fading at the ends of the fade:
    if (brightness == 0 || brightness == 300) {
      fadeAmount = -fadeAmount ;
    }
    delay(300);
    
    if (brightness == 0) {
      completeFades--;
    }
  }
}
  
// HELPER FUNCTIONS
// turns all red LED on
void redon() {
  digitalWrite(8, HIGH);   // turn the LED on (HIGH is the voltage level)
  digitalWrite(9, HIGH);   // turn the LED on (HIGH is the voltage level)
  digitalWrite(10, HIGH);   // turn the LED on (HIGH is the voltage level)
  digitalWrite(11, HIGH);   // turn the LED on (HIGH is the voltage level)
  digitalWrite(12, HIGH);   // turn the LED on (HIGH is the voltage level)
}
// turns all red LED off
void redoff() {
  digitalWrite(8, LOW);   // turn the LED off (LOW is the voltage level)
  digitalWrite(9, LOW);   // turn the LED off (LOW is the voltage level)
  digitalWrite(10, LOW);   // turn the LED off (LOW is the voltage level)
  digitalWrite(11, LOW);   // turn the LED off (LOW is the voltage level)
  digitalWrite(12, LOW);   // turn the LED off (LOW is the voltage level)
}
// turns all blue LED on
void blueon() {
  digitalWrite(3, HIGH);   // turn the LED on (HIGH is the voltage level)
  digitalWrite(4, HIGH);   // turn the LED on (HIGH is the voltage level)
  digitalWrite(5, HIGH);   // turn the LED on (HIGH is the voltage level)
  digitalWrite(6, HIGH);   // turn the LED on (HIGH is the voltage level)
  digitalWrite(7, HIGH);   // turn the LED on (HIGH is the voltage level)
}
// turns all blue LED off
void blueoff() {
  digitalWrite(3, LOW);   // turn the LED off (LOW is the voltage level)
  digitalWrite(4, LOW);   // turn the LED off (LOW is the voltage level)
  digitalWrite(5, LOW);   // turn the LED off (LOW is the voltage level)
  digitalWrite(6, LOW);   // turn the LED off (LOW is the voltage level)
  digitalWrite(7, LOW);   // turn the LED off (LOW is the voltage level)
}

void redSet(int brightness) {
  analogWrite(8, brightness);
  analogWrite(9, brightness);
  analogWrite(10, brightness);
  analogWrite(11, brightness);
  analogWrite(12, brightness);
}

void blueSet(int brightness) {
  analogWrite(3, brightness);
  analogWrite(4, brightness);
  analogWrite(5, brightness);
  analogWrite(6, brightness);
  analogWrite(7, brightness);
}
